// Logisim project Classlib.circ as structural Verilog: 12 circuits, main circuit HA_1
module HA_1 (
  input  A,
  input  B,
  output COUT__AB,
  output SUM__AB_prime__A_prime_B
);

  wire A_prime_B_out, AB_prime_out, not_1_out, not_2_out;

  not not_1 (not_1_out, B);
  not not_2 (not_2_out, A);
  and AB_prime (AB_prime_out, A, not_1_out);
  and A_prime_B (A_prime_B_out, not_2_out, B);
  and AB (COUT__AB, B, A);
  or or_1 (SUM__AB_prime__A_prime_B, AB_prime_out, A_prime_B_out);
endmodule

module FA_1 (
  input  A,
  input  Cin,
  input  B,
  output SUM,
  output Cout
);

  wire AB_out, XAB_out, XABC_out;

  and AB (AB_out, B, A);
  xor XAB (XAB_out, A, B);
  xor XABXC (SUM, Cin, XAB_out);
  and XABC (XABC_out, Cin, XAB_out);
  or or_1 (Cout, XABC_out, AB_out);
endmodule

module FA_4 (
  input  A0,
  input  A1,
  input  A2,
  input  A3,
  input  B0,
  input  B1,
  input  B2,
  input  B3,
  input  CIN,
  output S0,
  output S1,
  output S2,
  output S3,
  output COUT
);

  wire fa_1_1_cout, fa_1_2_cout, fa_1_3_cout;

  FA_1 fa_1_1 (.A(A0), .Cin(CIN), .B(B0), .SUM(S0), .Cout(fa_1_1_cout));
  FA_1 fa_1_2 (.A(A1), .Cin(fa_1_1_cout), .B(B1), .SUM(S1), .Cout(fa_1_2_cout));
  FA_1 fa_1_3 (.A(A2), .Cin(fa_1_2_cout), .B(B2), .SUM(S2), .Cout(fa_1_3_cout));
  FA_1 fa_1_4 (.A(A3), .Cin(fa_1_3_cout), .B(B3), .SUM(S3), .Cout(COUT));

  // Notes on the sheet:
  //   Full Adder
endmodule

// B
module INC_4 (
  input  CIN,
  input  A0,
  input  A1,
  input  A2,
  input  A3,
  output COUT,
  output S0,
  output S1,
  output S2,
  output S3
);

  wire ha_1_1_cout__ab, ha_1_2_cout__ab, ha_1_3_cout__ab;

  HA_1 ha_1_1 (.A(CIN), .B(A0), .COUT__AB(ha_1_1_cout__ab), .SUM__AB_prime__A_prime_B(S0));
  HA_1 ha_1_2 (.A(ha_1_1_cout__ab), .B(A1), .COUT__AB(ha_1_2_cout__ab), .SUM__AB_prime__A_prime_B(S1));
  HA_1 ha_1_3 (.A(ha_1_2_cout__ab), .B(A2), .COUT__AB(ha_1_3_cout__ab), .SUM__AB_prime__A_prime_B(S2));
  HA_1 ha_1_4 (.A(ha_1_3_cout__ab), .B(A3), .COUT__AB(COUT), .SUM__AB_prime__A_prime_B(S3));

  // Notes on the sheet:
  //   4-Bit Increment Schematic
endmodule

module Negate (
  input  PASS_prime_2_sCOMP,
  input  in_2,
  input  in_3,
  input  in_4,
  input  in_5,
  output out_6,
  output out_7,
  output out_8,
  output out_9,
  output out_10
);

  wire xor_1_out, xor_2_out, xor_3_out, xor_4_out;

  xor xor_1 (xor_1_out, PASS_prime_2_sCOMP, in_2);
  xor xor_2 (xor_2_out, PASS_prime_2_sCOMP, in_3);
  xor xor_3 (xor_3_out, PASS_prime_2_sCOMP, in_4);
  xor xor_4 (xor_4_out, PASS_prime_2_sCOMP, in_5);
  INC_4 inc_4_1 (
    .CIN(PASS_prime_2_sCOMP), .A0(xor_4_out), .A1(xor_3_out), .A2(xor_2_out), .A3(xor_1_out), .COUT(out_6),
    .S0(out_7), .S1(out_8), .S2(out_9), .S3(out_10));
endmodule

module MUX_1 (
  input  A,
  input  A_B_prime,
  input  B,
  output Y
);

  wire and_1_out, and_2_out, not_1_out;

  and and_1 (and_1_out, A, A_B_prime);
  not not_1 (not_1_out, A_B_prime);
  and and_2 (and_2_out, not_1_out, B);
  or or_1 (Y, and_1_out, and_2_out);
endmodule

module MUX_4 (
  input  S,
  input  A3,
  input  B3,
  input  A2,
  input  B2,
  input  A1,
  input  B1,
  input  A0,
  input  B0,
  output Y3,
  output Y2,
  output Y1,
  output Y0
);

  MUX_1 mux_1_1 (.A(A3), .A_B_prime(S), .B(B3), .Y(Y3));
  MUX_1 mux_1_2 (.A(A2), .A_B_prime(S), .B(B2), .Y(Y2));
  MUX_1 mux_1_3 (.A(A1), .A_B_prime(S), .B(B1), .Y(Y1));
  MUX_1 mux_1_4 (.A(A0), .A_B_prime(S), .B(B0), .Y(Y0));

  // Notes on the sheet:
  //   MUX_4 A/B' = 0, A = 12, B = 7
endmodule

module DEMUX_1 (
  input  I,
  input  S,
  output A,
  output B
);

  and and_1 (A, I, S);
  and and_2 (B, I, ~S);  // AND_Gate

  // Notes on the sheet:
  //   1-Bit Demultiplexer SOP Form
  //   I = IN
  //   S = Switch (A/B')
endmodule

module DEMUX_4 (
  input  D3,
  input  D2,
  input  D1,
  input  D0,
  input  A_B,
  output A3,
  output B3,
  output A2,
  output B2,
  output A1,
  output B1,
  output A0,
  output B0
);

  DEMUX_1 demux_1_1 (.S(A_B), .B(B3), .I(D3), .A(A3));
  DEMUX_1 demux_1_2 (.S(A_B), .B(B2), .I(D2), .A(A2));
  DEMUX_1 demux_1_3 (.S(A_B), .B(B1), .I(D1), .A(A1));
  DEMUX_1 demux_1_4 (.S(A_B), .B(B0), .I(D0), .A(A0));
endmodule

// ADD_SUB
module ADD_SUBT (
  input  Switch,
  input  B3,
  input  B2,
  input  B1,
  input  B0,
  input  A3,
  input  A2,
  input  A1,
  input  A0,
  output S3,
  output S2,
  output S1,
  output S0,
  output out_14
);

  wire inc_4_1_s0, inc_4_1_s1, inc_4_1_s2, inc_4_1_s3, xor_1_out, xor_2_out, xor_3_out, xor_4_out;

  xor xor_1 (xor_1_out, Switch, B3);
  xor xor_2 (xor_2_out, Switch, B2);
  xor xor_3 (xor_3_out, Switch, B1);
  xor xor_4 (xor_4_out, Switch, B0);
  INC_4 inc_4_1 (
    .CIN(Switch), .A0(xor_4_out), .A1(xor_3_out), .A2(xor_2_out), .A3(xor_1_out), .S0(inc_4_1_s0),
    .S1(inc_4_1_s1), .S2(inc_4_1_s2), .S3(inc_4_1_s3));  // open: COUT
  FA_4 fa_4_1 (
    .CIN(1'b0), .A0(inc_4_1_s0), .A1(inc_4_1_s1), .B0(A0), .B1(A1), .A2(inc_4_1_s2), .B2(A2),
    .A3(inc_4_1_s3), .B3(A3), .S0(S0), .S1(S1), .S2(S2), .S3(S3), .COUT(out_14));
  Hex_Digit_Display hex_digit_display_1 (.value({S3, S2, S1, S0}));  // open: dp

  // Notes on the sheet:
  //   +|- : 0|1
  //   Format goes X = A + B or A - B, order matters!
  //   If 1 = 0001, Bits go A3;A2:A1:A0
endmodule

module SHIFT (
  input  SHAMT1,
  input  SHAMT0,
  input  L_R_prime,
  input  SHNUM3,
  input  SHNUM2,
  input  SHNUM1,
  input  SHNUM0,
  output SHOUT3,
  output SHOUT2,
  output SHOUT1,
  output SHOUT0
);

  wire and_1_out, and_2_out, and_3_out, mux_4_1_y0, mux_4_1_y1, mux_4_1_y2, mux_4_1_y3, mux_4_2_y0,
       mux_4_2_y1, mux_4_2_y2, mux_4_2_y3, mux_4_3_y0, mux_4_3_y1, mux_4_3_y2, mux_4_3_y3, mux_4_4_y0,
       mux_4_4_y1, mux_4_4_y2, mux_4_4_y3, mux_4_5_y0, mux_4_5_y1, mux_4_5_y2, mux_4_5_y3, mux_4_6_y0,
       mux_4_6_y1, mux_4_6_y2, mux_4_6_y3, not_1_out, not_2_out, or_1_out, or_2_out;

  and and_1 (and_1_out, SHAMT0, not_1_out);
  not not_1 (not_1_out, SHAMT1);
  not not_2 (not_2_out, SHAMT0);
  and and_2 (and_2_out, not_2_out, SHAMT1);
  and and_3 (and_3_out, SHAMT1, SHAMT0);
  MUX_4 mux_4_1 (
    .A3(SHNUM2), .B3(SHNUM3), .A2(SHNUM1), .B2(SHNUM2), .A1(SHNUM0), .B1(SHNUM1), .A0(1'b0), .B0(SHNUM0),
    .Y3(mux_4_1_y3), .Y2(mux_4_1_y2), .Y1(mux_4_1_y1), .Y0(mux_4_1_y0), .S(or_2_out));
  MUX_4 mux_4_2 (
    .A3(1'b0), .B3(SHNUM3), .A2(SHNUM3), .B2(SHNUM2), .A1(SHNUM2), .B1(SHNUM1), .A0(SHNUM1), .B0(SHNUM0),
    .Y3(mux_4_2_y3), .Y2(mux_4_2_y2), .Y1(mux_4_2_y1), .Y0(mux_4_2_y0), .S(or_2_out));
  LED led_1 (.in(and_3_out));
  LED led_2 (.in(and_2_out));
  LED led_3 (.in(and_1_out));
  or or_1 (or_1_out, and_3_out, and_2_out);
  or or_2 (or_2_out, and_2_out, and_1_out, and_3_out);
  MUX_4 mux_4_3 (
    .A3(mux_4_1_y2), .B3(mux_4_1_y3), .A2(mux_4_1_y1), .B2(mux_4_1_y2), .A1(mux_4_1_y0), .B1(mux_4_1_y1),
    .A0(1'b0), .B0(mux_4_1_y0), .Y3(mux_4_3_y3), .Y2(mux_4_3_y2), .Y1(mux_4_3_y1), .Y0(mux_4_3_y0),
    .S(or_1_out));
  MUX_4 mux_4_4 (
    .A3(1'b0), .B3(mux_4_2_y3), .A2(mux_4_2_y3), .B2(mux_4_2_y2), .A1(mux_4_2_y2), .B1(mux_4_2_y1),
    .A0(mux_4_2_y0), .B0(mux_4_2_y0), .Y3(mux_4_4_y3), .Y2(mux_4_4_y2), .Y1(mux_4_4_y1), .Y0(mux_4_4_y0),
    .S(or_1_out));
  LED led_4 (.in(and_3_out));
  LED led_5 (.in(or_2_out));
  LED led_6 (.in(or_1_out));
  MUX_4 mux_4_5 (
    .A3(mux_4_3_y2), .B3(mux_4_3_y3), .A2(mux_4_3_y1), .B2(mux_4_3_y2), .A1(mux_4_3_y0), .B1(mux_4_3_y1),
    .A0(1'b0), .B0(mux_4_3_y0), .Y3(mux_4_5_y3), .Y2(mux_4_5_y2), .Y1(mux_4_5_y1), .Y0(mux_4_5_y0),
    .S(and_3_out));
  MUX_4 mux_4_6 (
    .A3(1'b0), .B3(mux_4_4_y3), .A2(mux_4_4_y3), .B2(mux_4_4_y2), .A1(mux_4_4_y2), .B1(mux_4_4_y1),
    .A0(mux_4_4_y1), .B0(mux_4_4_y0), .Y3(mux_4_6_y3), .Y2(mux_4_6_y2), .Y1(mux_4_6_y1), .Y0(mux_4_6_y0),
    .S(and_3_out));
  MUX_4 mux_4_7 (
    .A3(mux_4_5_y3), .B3(mux_4_6_y3), .A2(mux_4_5_y2), .B2(mux_4_6_y2), .A1(mux_4_5_y1), .B1(mux_4_6_y1),
    .A0(mux_4_5_y0), .B0(mux_4_6_y0), .Y3(SHOUT3), .Y2(SHOUT2), .Y1(SHOUT1), .Y0(SHOUT0), .S(L_R_prime));
endmodule

module Multiply (
  input  MD3,
  input  MD2,
  input  MD1,
  input  MD0,
  input  MR3,
  input  MR2,
  input  MR1,
  input  MR0,
  output PR7,
  output PR6,
  output PR5,
  output PR4,
  output PR3,
  output PR2,
  output PR1,
  output PR0
);

  wire add_subt_1_s0, add_subt_1_s1, add_subt_1_s2, add_subt_1_s3, add_subt_2_p14, add_subt_2_p15,
       add_subt_2_p16, add_subt_2_p17, fa_4_1_s0, fa_4_1_s1, fa_4_1_s2, fa_4_1_s3, fa_4_3_p8, fa_4_3_p9,
       fa_4_3_p10, fa_4_3_p11, fa_4_3_p12, fa_4_3_p13, fa_4_4_p11, fa_4_4_p12, fa_4_4_p13, fa_4_4_p14,
       fa_4_5_p9, fa_4_5_p10, fa_4_5_p11, fa_4_5_p12, fa_4_5_p13, fa_4_6_p11, fa_4_6_p12, fa_4_6_p13,
       fa_4_6_p14, fa_4_7_p9, fa_4_7_p10, fa_4_7_p11, fa_4_7_p12, fa_4_7_p13, fa_4_8_p11, fa_4_8_p12,
       fa_4_8_p13, fa_4_8_p14, fa_4_9_p9, mux_4_1_y0, mux_4_1_y1, mux_4_1_y2, mux_4_1_y3, undriven,
       undriven_2, xor_1_out, xor_2_out, xor_3_out, xor_4_out, xor_5_out, xor_6_out, xor_7_out, xor_8_out,
       xor_9_out;
  wire [3:0] add_subt_2_p13, fa_4_4_p4, mux_4_2_p13, mux_4_3_p13, mux_4_4_p13, mux_4_5_p13, mux_4_6_p13,
       mux_4_7_p13;

  Hex_Digit_Display hex_digit_display_1 (.value({MR3, MR2, MR1, MR0}));  // open: dp
  Hex_Digit_Display hex_digit_display_2 (.value({MD3, MD2, MD1, MD0}));  // open: dp
  ADD_SUBT add_subt_1 (
    .Switch(MD3), .B3(MD3), .B2(MD2), .B1(MD1), .B0(MD0), .A3(1'b0), .A2(1'b0), .A1(1'b0), .A0(1'b0),
    .S3(add_subt_1_s3), .S2(add_subt_1_s2), .S1(add_subt_1_s1), .S0(add_subt_1_s0));  // open: out_14
  // Add_Subt add_subt_2: pin names not known; wires that end beside it: MR3, MR3, MR2, MR1, MR0, 1'b0, 1'b0, 1'b0, 1'b0, add_subt_2_p13[3], add_subt_2_p13[2], add_subt_2_p13[1], add_subt_2_p13[0], add_subt_2_p14, add_subt_2_p15, add_subt_2_p16, add_subt_2_p17
  Hex_Digit_Display hex_digit_display_3 (.value(add_subt_2_p13));  // open: dp
  FA_4 fa_4_1 (
    .CIN(1'b0), .A0(1'b0), .A1(1'b0), .B0(add_subt_1_s0), .B1(add_subt_1_s1), .A2(1'b0), .B2(add_subt_1_s2),
    .A3(1'b0), .B3(add_subt_1_s3), .S0(fa_4_1_s0), .S1(fa_4_1_s1), .S2(fa_4_1_s2), .S3(fa_4_1_s3));  // open: COUT
  MUX_4 mux_4_1 (
    .A3(fa_4_1_s3), .B3(1'b0), .A2(fa_4_1_s2), .B2(1'b0), .A1(fa_4_1_s1), .B1(1'b0), .A0(fa_4_1_s0),
    .B0(1'b0), .Y3(mux_4_1_y3), .Y2(mux_4_1_y2), .Y1(mux_4_1_y1), .Y0(mux_4_1_y0), .S(undriven_2));
  LED led_1 (.in(add_subt_2_p13[0]));
  FA_4 fa_4_2 (
    .CIN(1'b0), .A0(mux_4_1_y0), .A1(mux_4_1_y1), .B0(1'b0), .A2(mux_4_1_y2), .A3(mux_4_1_y3));  // open: B1, B2, B3, S0, S1, S2, S3, COUT
  // NOTMINE_FA_4 fa_4_3: pin names not known; wires that end beside it: 1'b0, 1'b0, 1'b0, 1'b0, 1'b0, 1'b0, 1'b0, fa_4_3_p8, fa_4_3_p9, fa_4_3_p10, fa_4_3_p11, fa_4_3_p12, fa_4_3_p13
  // NOTMINE_FA_4 fa_4_4: pin names not known; wires that end beside it: fa_4_4_p4[3], fa_4_4_p4[2], fa_4_4_p4[1], fa_4_4_p4[0], add_subt_2_p15, add_subt_2_p16, add_subt_2_p17, 1'b0, 1'b0, fa_4_3_p9, fa_4_4_p11, fa_4_4_p12, fa_4_4_p13, fa_4_4_p14
  Hex_Digit_Display hex_digit_display_4 (.value(fa_4_4_p4));  // open: dp
  LED led_2 (.in(add_subt_2_p13[1]));
  // NOTMINE_MUX_4 mux_4_2: pin names not known; wires that end beside it: fa_4_3_p10, fa_4_3_p11, fa_4_3_p12, fa_4_3_p13, 1'b0, 1'b0, 1'b0, 1'b0, add_subt_2_p13[1], mux_4_2_p13[3], mux_4_2_p13[2], mux_4_2_p13[1], mux_4_2_p13[0]
  // NOTMINE_MUX_4 mux_4_3: pin names not known; wires that end beside it: fa_4_4_p11, fa_4_4_p12, fa_4_4_p13, fa_4_4_p14, fa_4_4_p4[3], fa_4_4_p4[2], fa_4_4_p4[1], fa_4_4_p4[0], add_subt_2_p13[1], mux_4_3_p13[3], mux_4_3_p13[2], mux_4_3_p13[1], mux_4_3_p13[0]
  // NOTMINE_FA_4 fa_4_5: pin names not known; wires that end beside it: mux_4_2_p13[3], mux_4_2_p13[2], mux_4_2_p13[1], mux_4_2_p13[0], 1'b0, 1'b0, add_subt_2_p14, add_subt_2_p15, fa_4_5_p9, fa_4_5_p10, fa_4_5_p11, fa_4_5_p12, fa_4_5_p13
  // NOTMINE_FA_4 fa_4_6: pin names not known; wires that end beside it: mux_4_3_p13[3], mux_4_3_p13[2], mux_4_3_p13[1], mux_4_3_p13[0], add_subt_2_p16, add_subt_2_p17, 1'b0, 1'b0, 1'b0, fa_4_5_p9, fa_4_6_p11, fa_4_6_p12, fa_4_6_p13, fa_4_6_p14
  Hex_Digit_Display hex_digit_display_5 (.value(mux_4_2_p13));  // open: dp
  // NOTMINE_MUX_4 mux_4_4: pin names not known; wires that end beside it: fa_4_5_p10, fa_4_5_p11, fa_4_5_p12, fa_4_5_p13, mux_4_2_p13[3], mux_4_2_p13[2], mux_4_2_p13[1], mux_4_2_p13[0], add_subt_2_p13[2], mux_4_4_p13[3], mux_4_4_p13[2], mux_4_4_p13[1], mux_4_4_p13[0]
  // NOTMINE_MUX_4 mux_4_5: pin names not known; wires that end beside it: fa_4_6_p11, fa_4_6_p12, fa_4_6_p13, fa_4_6_p14, mux_4_3_p13[3], mux_4_3_p13[2], mux_4_3_p13[1], mux_4_3_p13[0], add_subt_2_p13[2], mux_4_5_p13[3], mux_4_5_p13[2], mux_4_5_p13[1], mux_4_5_p13[0]
  Hex_Digit_Display hex_digit_display_6 (.value(mux_4_3_p13));  // open: dp
  LED led_3 (.in(add_subt_2_p13[2]));
  xor xor_1 (xor_1_out, undriven, MR3);
  Hex_Digit_Display hex_digit_display_7 (.value(mux_4_4_p13));  // open: dp
  // NOTMINE_FA_4 fa_4_7: pin names not known; wires that end beside it: mux_4_4_p13[3], mux_4_4_p13[2], mux_4_4_p13[1], mux_4_4_p13[0], 1'b0, add_subt_2_p14, add_subt_2_p15, add_subt_2_p16, fa_4_7_p9, fa_4_7_p10, fa_4_7_p11, fa_4_7_p12, fa_4_7_p13
  // NOTMINE_FA_4 fa_4_8: pin names not known; wires that end beside it: mux_4_5_p13[3], mux_4_5_p13[2], mux_4_5_p13[1], mux_4_5_p13[0], add_subt_2_p17, 1'b0, 1'b0, 1'b0, 1'b0, fa_4_7_p9, fa_4_8_p11, fa_4_8_p12, fa_4_8_p13, fa_4_8_p14
  Hex_Digit_Display hex_digit_display_8 (.value(mux_4_5_p13));  // open: dp
  Hex_Digit_Display hex_digit_display_9 (.value(mux_4_6_p13));  // open: dp
  // NOTMINE_MUX_4 mux_4_6: pin names not known; wires that end beside it: fa_4_7_p10, fa_4_7_p11, fa_4_7_p12, fa_4_7_p13, mux_4_4_p13[3], mux_4_4_p13[2], mux_4_4_p13[1], mux_4_4_p13[0], add_subt_2_p13[3], mux_4_6_p13[3], mux_4_6_p13[2], mux_4_6_p13[1], mux_4_6_p13[0]
  // NOTMINE_MUX_4 mux_4_7: pin names not known; wires that end beside it: fa_4_8_p11, fa_4_8_p12, fa_4_8_p13, fa_4_8_p14, mux_4_5_p13[3], mux_4_5_p13[2], mux_4_5_p13[1], mux_4_5_p13[0], add_subt_2_p13[3], mux_4_7_p13[3], mux_4_7_p13[2], mux_4_7_p13[1], mux_4_7_p13[0]
  LED led_4 (.in(add_subt_2_p13[3]));
  Hex_Digit_Display hex_digit_display_10 (.value(mux_4_7_p13));  // open: dp
  xor xor_2 (xor_2_out, xor_1_out, mux_4_6_p13[3]);
  xor xor_3 (xor_3_out, xor_1_out, mux_4_6_p13[2]);
  xor xor_4 (xor_4_out, xor_1_out, mux_4_6_p13[1]);
  xor xor_5 (xor_5_out, xor_1_out, mux_4_6_p13[0]);
  xor xor_6 (xor_6_out, xor_1_out, mux_4_7_p13[3]);
  xor xor_7 (xor_7_out, xor_1_out, mux_4_7_p13[2]);
  xor xor_8 (xor_8_out, xor_1_out, mux_4_7_p13[1]);
  xor xor_9 (xor_9_out, xor_1_out, mux_4_7_p13[0]);
  // NOTMINE_FA_4 fa_4_9: pin names not known; wires that end beside it: 1'b0, 1'b0, 1'b0, 1'b0, xor_2_out, xor_3_out, xor_4_out, xor_5_out, fa_4_9_p9, PR7, PR6, PR5, PR4
  // NOTMINE_FA_4 fa_4_10: pin names not known; wires that end beside it: 1'b0, 1'b0, 1'b0, 1'b0, xor_6_out, xor_7_out, xor_8_out, xor_9_out, xor_1_out, fa_4_9_p9, PR3, PR2, PR1, PR0
  Hex_Digit_Display hex_digit_display_11 (.value({PR7, PR6, PR5, PR4}));  // open: dp
  Hex_Digit_Display hex_digit_display_12 (.value({PR3, PR2, PR1, PR0}));  // open: dp
endmodule
